// Logisim project SLIS_COM1.circ as structural Verilog
module _1bit_ADDER (
  input  in_1,
  input  in_2,
  input  in_3,
  output out_4,
  output out_5
);

  wire and_1_out, and_2_out, xor_1_out;

  and and_1 (and_1_out, in_1, in_2);
  xor xor_1 (xor_1_out, in_1, in_2);
  and and_2 (and_2_out, xor_1_out, in_3);
  xor xor_2 (out_5, xor_1_out, in_3);
  or or_1 (out_4, and_1_out, and_2_out);

  // Notes on the sheet:
  //   ADDR
endmodule

module _8bit_ADDER (
  input  [7:0] in_1,
  input  [7:0] in_2,
  input  in_3,
  output [7:0] out_4,
  output out_5
);

  wire n1bit_adder_1_out_4, n1bit_adder_2_out_4, n1bit_adder_3_out_4, n1bit_adder_4_out_4,
       n1bit_adder_5_out_4, n1bit_adder_6_out_4, n1bit_adder_7_out_4;

  _1bit_ADDER u_1bit_adder_1 (
    .out_4(n1bit_adder_1_out_4), .in_1(in_2[7]), .in_2(in_1[7]), .out_5(out_4[7]), .in_3(in_3));
  _1bit_ADDER u_1bit_adder_2 (
    .out_4(n1bit_adder_2_out_4), .in_1(in_2[6]), .in_2(in_1[6]), .out_5(out_4[6]), .in_3(n1bit_adder_1_out_4));
  _1bit_ADDER u_1bit_adder_3 (
    .out_4(n1bit_adder_3_out_4), .in_1(in_2[5]), .in_2(in_1[5]), .out_5(out_4[5]), .in_3(n1bit_adder_2_out_4));
  _1bit_ADDER u_1bit_adder_4 (
    .out_4(n1bit_adder_4_out_4), .in_1(in_2[4]), .in_2(in_1[4]), .out_5(out_4[4]), .in_3(n1bit_adder_3_out_4));
  _1bit_ADDER u_1bit_adder_5 (
    .out_4(n1bit_adder_5_out_4), .in_1(in_2[3]), .in_2(in_1[3]), .out_5(out_4[3]), .in_3(n1bit_adder_4_out_4));
  _1bit_ADDER u_1bit_adder_6 (
    .out_4(n1bit_adder_6_out_4), .in_1(in_2[2]), .in_2(in_1[2]), .out_5(out_4[2]), .in_3(n1bit_adder_5_out_4));
  _1bit_ADDER u_1bit_adder_7 (
    .out_4(n1bit_adder_7_out_4), .in_1(in_2[1]), .in_2(in_1[1]), .out_5(out_4[1]), .in_3(n1bit_adder_6_out_4));
  _1bit_ADDER u_1bit_adder_8 (
    .out_4(out_5), .in_1(in_2[0]), .in_2(in_1[0]), .out_5(out_4[0]), .in_3(n1bit_adder_7_out_4));

  // Notes on the sheet:
  //   BIT ALIGN CHECK!!
endmodule

module OpTypeDecoder (
  input  [1:0] in_1,
  output out_2,
  output out_3,
  output out_4,
  output out_5
);

  wire not_1_out, not_2_out;

  not not_1 (not_1_out, in_1[1]);
  not not_2 (not_2_out, in_1[0]);
  and and_1 (out_2, not_2_out, not_1_out);
  and and_2 (out_3, in_1[0], not_1_out);
  and and_3 (out_4, not_2_out, in_1[1]);
  and and_4 (out_5, in_1[0], in_1[1]);
endmodule

module ALU (
  input  Ci,
  input  [7:0] DATA_IN_1,
  input  [7:0] DATA_IN_2,
  input  ALU_ACTIVE,
  input  [1:0] OPCODE,
  output Co,
  output [7:0] Data_Out
);

  wire [7:0] demultiplexer_1_out0, demultiplexer_2_out0;

  Demultiplexer #(.select(2), .width(8)) demultiplexer_1 (
    .out0(demultiplexer_1_out0), .in(DATA_IN_1), .sel(OPCODE), .en(ALU_ACTIVE));  // open: out1, out2, out3
  Demultiplexer #(.select(2), .width(8)) demultiplexer_2 (
    .out0(demultiplexer_2_out0), .in(DATA_IN_2), .sel(OPCODE), .en(ALU_ACTIVE));  // open: out1, out2, out3
  _8bit_ADDER u_8bit_adder_1 (
    .in_1(demultiplexer_1_out0), .in_2(demultiplexer_2_out0), .in_3(Ci), .out_5(Co), .out_4(Data_Out));
endmodule

module StateRegister (
);

  wire undriven_2, undriven_3;
  wire [7:0] register_1_q, undriven;

  Register register_1 (.D(undriven), .en(undriven_2), .Q(register_1_q), .clk(undriven_3));  // open: clr
endmodule
